# Fritzing sketch ir transmitterV2 (saved by Fritzing 0.9.1b)
breadboards: 1

parts:
  D1 = LTE-302 [package=lte-302]
  R1 = Resistor [tolerance=±5% resistance=2.2k package=THT]
  Part2 = Thumb Joystick
  R2 = Resistor [tolerance=±5% resistance=10k package="0805 [SMD]"]
  Pin_D3 = female pin header, 1 pin [form="♀ (female)"]
  Pin_D13 = female pin header, 1 pin [form="♀ (female)"]

nets:
  N1: D1.A, R1.Pin_1
  N2: D1.C, Part2.GND
  N3: R1.Pin_0, Pin_D13.pin1
  N4: Part2.SEL, R2.Pin_1, Pin_D3.pin1
  N5: Part2.VCC, R2.Pin_0
