# Fritzing sketch joystick (saved by Fritzing 0.9.1b)
breadboards: 1

parts:
  Part2 = Thumb Joystick
  D1 = LTE-302 [package=lte-302]
  J1 = Basic Servo
  R1 = Resistor [tolerance=±5% resistance=10k package=THT]
  R2 = Resistor [tolerance=±5% resistance=2.2k package=THT]
  Pin_A0 = female pin header, 1 pin [form="♀ (female)"]
  Pin_D13 = female pin header, 1 pin [form="♀ (female)"]
  Pin_D9 = female pin header, 1 pin [form="♀ (female)"]
  Pin_D3 = female pin header, 1 pin [form="♀ (female)"]  # not connected

nets:
  GND: Part2.GND, D1.C, J1.gnd
  N1: Part2.SEL, R1.Pin_1
  N2: Part2.HORZ, Pin_A0.pin1
  5V: Part2.VCC, J1.vcc, R1.Pin_0
  N3: D1.A, R2.Pin_1
  N4: J1.pulse, Pin_D9.pin1
  N5: R2.Pin_0, Pin_D13.pin1
