# Fritzing sketch project1 (saved by Fritzing 0.9.1b)
breadboards: 1

parts:
  Part1 = Arduino Mega 2560 (Rev3)
  J1 = Basic Servo
  R3 = Resistor [tolerance=±5% resistance=10k package=THT]
  R4 = Resistor [tolerance=±5% resistance=2.2k package=THT]
  Part2 = Thumb Joystick
  Part3 = Breadboard Power Supply Board SMD
  D1 = LTE-302 [package=lte-302]

nets:
  N1: Part1.A0, Part2.VERT
  N2: Part1.D13_PWM, R4.Pin_0
  N3: Part1.D9_PWM, J1.pulse
  GND: Part1.GND, J1.gnd, Part2.GND, Part3.GND, D1.C
  N4: Part1.D3_PWM, R3.Pin_1, Part2.SEL
  VCC: J1.vcc, R3.Pin_0, Part2.VCC, Part3.VCC
  N5: R4.Pin_1, D1.A
