# Fritzing sketch servo (saved by Fritzing 0.9.1b)
breadboards: 1

parts:
  Part2 = Thumb Joystick
  J1 = Basic Servo
  Pin_A0 = female pin header, 1 pin [form="♀ (female)"]
  Pin_D9 = female pin header, 1 pin [form="♀ (female)"]

nets:
  GND: Part2.GND, J1.gnd
  N1: Part2.VERT, Pin_D9.pin1
  VCC: Part2.VCC, J1.vcc
  N2: J1.pulse, Pin_A0.pin1
